// Logisim project 16-bit.circ as structural Verilog: 12 circuits, main circuit main
module main (
  input  Reset_RAM,
  input  Reset_System,
  output [15:0] _7_Segment_Output
);

  wire and_1_out, Clock_out, instruction_set_1_ai, instruction_set_1_ao, instruction_set_1_bi,
       instruction_set_1_bo, instruction_set_1_cd, instruction_set_1_ce, instruction_set_1_ci,
       instruction_set_1_co, instruction_set_1_co_2, instruction_set_1_eo, instruction_set_1_fi,
       instruction_set_1_hl, instruction_set_1_ii, instruction_set_1_jp, instruction_set_1_mi,
       instruction_set_1_oi, instruction_set_1_rr, instruction_set_1_rw, instruction_set_1_su,
       instruction_set_1_wd, or_1_out, or_2_out;
  wire [1:0] alu_1_zf, register_2bit_1_do, register_2bit_1_oo;
  wire [3:0] display_instruction_set_1_position_output;
  wire [6:0] display_instruction_set_1_acsii_output;
  wire [15:0] adder_1_out, counter_1_do, display_instruction_set_1_full_output, display_register_1_out_7,
       display_register_1_out_8, display_register_1_out_9, display_register_1_out_10,
       display_register_1_out_11, display_register_1_out_12, display_register_1_out_13,
       display_register_1_out_14, display_register_1_out_15, display_register_1_out_16,
       display_register_1_out_17, display_register_1_out_18, display_register_1_out_19,
       display_register_1_out_20, display_register_1_out_21, display_register_1_out_22, register_1_oo,
       register_2_oo, register_3_do, register_4_do, register_5_oo;

  Clock Clock (.out(Clock_out));
  register register_1 (
    .Ii(register_2_oo), .load(instruction_set_1_ii), .clock(and_1_out), .clear(Reset_System), .enable(1'b1),
    .Oo(register_1_oo));  // open: Do
  and and_1 (and_1_out, ~instruction_set_1_hl, ~Reset_System, Clock_out);  // AND_Gate
  Adder #(.width(16)) adder_1 (.a(register_2_oo), .b(16'h1), .out(adder_1_out));  // open: cin, cout
  instruction_set instruction_set_1 (
    .ZF(register_2bit_1_oo[0]), .CF(register_2bit_1_oo[1]), .OP0(register_1_oo[0]), .OP1(register_1_oo[1]),
    .OP2(register_1_oo[2]), .OP3(register_1_oo[3]), .OP4(register_1_oo[4]), .Clear(Reset_System),
    .Clock(and_1_out), .OI(instruction_set_1_oi), .JP(instruction_set_1_jp), .CO(instruction_set_1_co),
    .CE(instruction_set_1_ce), .II(instruction_set_1_ii), .RR(instruction_set_1_rr),
    .RW(instruction_set_1_rw), .MI(instruction_set_1_mi), .BO(instruction_set_1_bo),
    .BI(instruction_set_1_bi), .SU(instruction_set_1_su), .EO(instruction_set_1_eo),
    .AO(instruction_set_1_ao), .AI(instruction_set_1_ai), .HL(instruction_set_1_hl),
    .FI(instruction_set_1_fi), .CO_2(instruction_set_1_co_2), .CI(instruction_set_1_ci),
    .WD(instruction_set_1_wd), .CD(instruction_set_1_cd));  // open: S7, S6, S5, S4, S3, S2, S1, S0, IR
  register register_2 (
    .Ii(adder_1_out), .load(instruction_set_1_ci), .clock(and_1_out), .clear(Reset_System),
    .enable(instruction_set_1_co_2), .Oo(register_2_oo));  // open: Do
  register register_3 (
    .Ii(register_2_oo), .load(instruction_set_1_ai), .clock(and_1_out), .clear(Reset_System),
    .enable(instruction_set_1_ao), .Do(register_3_do), .Oo(register_2_oo));
  register register_4 (
    .Ii(register_2_oo), .load(instruction_set_1_bi), .clock(and_1_out), .clear(Reset_System),
    .enable(instruction_set_1_bo), .Do(register_4_do), .Oo(register_2_oo));
  register register_5 (
    .Ii(register_2_oo), .load(instruction_set_1_mi), .clock(and_1_out), .clear(Reset_System), .enable(1'b1),
    .Oo(register_5_oo));  // open: Do
  register_2bit register_2bit_1 (
    .Ii(alu_1_zf), .Oo(register_2bit_1_oo), .Do(register_2bit_1_do), .clock(and_1_out),
    .load(instruction_set_1_fi), .reset(Reset_System), .enable(1'b1));
  alu alu_1 (
    .A(register_3_do), .B(register_4_do), .Oo(register_2_oo), .En(instruction_set_1_eo),
    .Su(instruction_set_1_su), .CF(alu_1_zf[1]), .ZF(alu_1_zf[0]));  // open: Do
  RAM #(.addrWidth(16), .dataWidth(16)) ram_1 (
    .addr(register_5_oo), .data(register_2_oo), .sel(or_1_out), .clk(and_1_out), .ld(instruction_set_1_rr),
    .clr(Reset_RAM));
  or or_1 (or_1_out, instruction_set_1_rw, instruction_set_1_rr);
  counter counter_1 (
    .CEnable(1'b1), .CReset(counter_1_do[4]), .clock(and_1_out), .Do(counter_1_do));  // open: COut, CWrite, Ii, Oo
  counter counter_2 (
    .COut(instruction_set_1_co), .CEnable(instruction_set_1_ce), .CWrite(instruction_set_1_jp),
    .CReset(Reset_System), .clock(and_1_out), .Ii(register_2_oo), .Oo(register_2_oo));  // open: Do
  register register_6 (
    .Ii(register_2_oo), .load(instruction_set_1_oi), .clock(and_1_out), .clear(Reset_System), .enable(1'b1),
    .Do(_7_Segment_Output));  // open: Oo
  display_instruction_set display_instruction_set_1 (
    .Clock(and_1_out), .Clear(Reset_System), .in_3(counter_1_do),
    .ACSII_Output(display_instruction_set_1_acsii_output),
    .Full_Output(display_instruction_set_1_full_output),
    .Position_Output(display_instruction_set_1_position_output));
  DotMatrix #(.matrixcols(16), .matrixrows(16)) dotmatrix_1 (
    .col0(display_register_1_out_7), .col1(display_register_1_out_8), .col2(display_register_1_out_9),
    .col3(display_register_1_out_10), .col4(display_register_1_out_11), .col5(display_register_1_out_12),
    .col6(display_register_1_out_13), .col7(display_register_1_out_14), .col8(display_register_1_out_15),
    .col9(display_register_1_out_16), .col10(display_register_1_out_17), .col11(display_register_1_out_18),
    .col12(display_register_1_out_19), .col13(display_register_1_out_20), .col14(display_register_1_out_21),
    .col15(display_register_1_out_22));
  display_register display_register_1 (
    .Clock(and_1_out), .Enabled(1'b1), .in_5(register_2_oo), .out_7(display_register_1_out_7),
    .out_8(display_register_1_out_8), .out_9(display_register_1_out_9), .out_10(display_register_1_out_10),
    .out_11(display_register_1_out_11), .out_12(display_register_1_out_12),
    .out_13(display_register_1_out_13), .out_14(display_register_1_out_14),
    .out_15(display_register_1_out_15), .out_16(display_register_1_out_16),
    .out_17(display_register_1_out_17), .out_18(display_register_1_out_18),
    .out_19(display_register_1_out_19), .out_20(display_register_1_out_20),
    .out_21(display_register_1_out_21), .out_22(display_register_1_out_22),
    .in_6(display_instruction_set_1_position_output));  // open: Clear, ClearAll
  TTY tty_1 (.data(display_instruction_set_1_acsii_output), .clk(and_1_out), .we(instruction_set_1_wd), .clr(or_2_out));
  or or_2 (or_2_out, Reset_System, instruction_set_1_cd);
endmodule

module register (
  input  [15:0] Ii,
  input  load,
  input  clock,
  input  clear,
  input  enable,
  output [15:0] Do,
  output [15:0] Oo
);

  assign Oo = enable ? Do : 16'bz;  // Controlled_Buffer controlled_buffer_1
  Register #(.width(16)) register_1 (.D(Ii), .en(load), .Q(Do), .clk(clock), .clr(clear));
endmodule

module full_adder (
  input  A,
  input  B,
  input  Ci,
  output E,
  output Co
);

  wire and_1_out, and_2_out, xor_1_out;

  xor xor_1 (xor_1_out, A, B);
  and and_1 (and_1_out, Ci, xor_1_out);
  and and_2 (and_2_out, A, B);
  xor xor_2 (E, xor_1_out, Ci);
  or or_1 (Co, and_1_out, and_2_out);
endmodule

module alu (
  input  [15:0] A,
  input  Su,
  input  En,
  input  [15:0] B,
  output CF,
  output ZF,
  output [15:0] Oo,
  output [15:0] Do
);

  wire full_adder_1_co, full_adder_2_co, full_adder_3_co, full_adder_4_co, full_adder_5_co, full_adder_6_co,
       full_adder_7_co, full_adder_8_co, full_adder_9_co, full_adder_10_co, full_adder_11_co,
       full_adder_12_co, full_adder_13_co, full_adder_14_co, full_adder_15_co, full_adder_16_co, xor_1_out,
       xor_2_out, xor_3_out, xor_4_out, xor_5_out, xor_6_out, xor_7_out, xor_8_out, xor_9_out, xor_10_out,
       xor_11_out, xor_12_out, xor_13_out, xor_14_out, xor_15_out, xor_16_out;

  full_adder full_adder_1 (.A(A[0]), .B(xor_1_out), .Ci(Su), .E(Do[0]), .Co(full_adder_1_co));
  full_adder full_adder_2 (.A(A[1]), .B(xor_2_out), .Ci(full_adder_1_co), .E(Do[1]), .Co(full_adder_2_co));
  xor xor_1 (xor_1_out, Su, B[0]);
  xor xor_2 (xor_2_out, Su, B[1]);
  full_adder full_adder_3 (.A(A[2]), .B(xor_4_out), .Ci(full_adder_2_co), .E(Do[2]), .Co(full_adder_3_co));
  xor xor_3 (xor_3_out, Su, B[3]);
  xor xor_4 (xor_4_out, Su, B[2]);
  full_adder full_adder_4 (.A(A[3]), .B(xor_3_out), .Ci(full_adder_3_co), .E(Do[3]), .Co(full_adder_4_co));
  full_adder full_adder_5 (.A(A[4]), .B(xor_5_out), .Ci(full_adder_4_co), .E(Do[4]), .Co(full_adder_5_co));
  xor xor_5 (xor_5_out, Su, B[4]);
  xor xor_6 (xor_6_out, Su, B[5]);
  full_adder full_adder_6 (.A(A[5]), .B(xor_6_out), .Ci(full_adder_5_co), .E(Do[5]), .Co(full_adder_6_co));
  xor xor_7 (xor_7_out, Su, B[7]);
  xor xor_8 (xor_8_out, Su, B[6]);
  full_adder full_adder_7 (.A(A[6]), .B(xor_8_out), .Ci(full_adder_6_co), .E(Do[6]), .Co(full_adder_7_co));
  xor xor_9 (xor_9_out, Su, B[9]);
  xor xor_10 (xor_10_out, Su, B[8]);
  full_adder full_adder_8 (.A(A[8]), .B(xor_10_out), .Ci(full_adder_9_co), .E(Do[8]), .Co(full_adder_8_co));
  full_adder full_adder_9 (.A(A[7]), .B(xor_7_out), .Ci(full_adder_7_co), .E(Do[7]), .Co(full_adder_9_co));
  xor xor_11 (xor_11_out, Su, B[10]);
  xor xor_12 (xor_12_out, Su, B[11]);
  full_adder full_adder_10 (.A(A[9]), .B(xor_9_out), .Ci(full_adder_8_co), .E(Do[9]), .Co(full_adder_10_co));
  xor xor_13 (xor_13_out, Su, B[13]);
  xor xor_14 (xor_14_out, Su, B[12]);
  full_adder full_adder_11 (.A(A[10]), .B(xor_11_out), .Ci(full_adder_10_co), .E(Do[10]), .Co(full_adder_11_co));
  xor xor_15 (xor_15_out, Su, B[14]);
  xor xor_16 (xor_16_out, Su, B[15]);
  full_adder full_adder_12 (.A(A[12]), .B(xor_14_out), .Ci(full_adder_13_co), .E(Do[12]), .Co(full_adder_12_co));
  full_adder full_adder_13 (.A(A[11]), .B(xor_12_out), .Ci(full_adder_11_co), .E(Do[11]), .Co(full_adder_13_co));
  full_adder full_adder_14 (.A(A[13]), .B(xor_13_out), .Ci(full_adder_12_co), .E(Do[13]), .Co(full_adder_14_co));
  full_adder full_adder_15 (.A(A[14]), .B(xor_15_out), .Ci(full_adder_14_co), .E(Do[14]), .Co(full_adder_15_co));
  xor xor_17 (CF, Su, full_adder_16_co);
  full_adder full_adder_16 (.A(A[15]), .B(xor_16_out), .Ci(full_adder_15_co), .E(Do[15]), .Co(full_adder_16_co));
  nor nor_1 (ZF, Do[15], Do[14], Do[13], Do[12], Do[11], Do[10], Do[9], Do[8], Do[7], Do[6], Do[5], Do[4], Do[3], Do[2], Do[1], Do[0]);
  assign Oo = En ? Do : 16'bz;  // Controlled_Buffer controlled_buffer_1
endmodule

module counter (
  input  COut,
  input  CEnable,
  input  CWrite,
  input  CReset,
  input  clock,
  input  [15:0] Ii,
  output [15:0] Oo,
  output [15:0] Do
);

  wire and_1_out, and_2_out, and_3_out, and_4_out, and_5_out, and_6_out, and_7_out, and_8_out, and_9_out,
       and_10_out, and_11_out, and_12_out, and_13_out, and_14_out, and_15_out, and_16_out, and_17_out,
       and_18_out, and_19_out, and_20_out, and_21_out, and_22_out, and_23_out, and_24_out, and_25_out,
       and_26_out, and_27_out, and_28_out, and_29_out, and_30_out, and_31_out, and_32_out, j_k_ff_2_qn,
       j_k_ff_3_qn, j_k_ff_4_qn, j_k_ff_5_qn, j_k_ff_6_qn, j_k_ff_7_qn, j_k_ff_8_qn, j_k_ff_9_qn,
       j_k_ff_10_qn, j_k_ff_11_qn, j_k_ff_12_qn, j_k_ff_13_qn, j_k_ff_14_qn, j_k_ff_15_qn, j_k_ff_16_qn,
       or_1_out, or_2_out, or_3_out, or_4_out, or_5_out, or_6_out, or_7_out, or_8_out, or_9_out, or_10_out,
       or_11_out, or_12_out, or_13_out, or_14_out, or_15_out, or_16_out;

  and and_1 (and_1_out, CWrite, Ii[15], clock);
  J_K_Flip_Flop j_k_ff_1 (
    .J(CEnable), .clk(j_k_ff_2_qn), .K(CEnable), .Q(Do[15]), .preset(and_1_out), .reset(or_1_out));  // open: Qn, en
  or or_1 (or_1_out, CReset, and_2_out);
  and and_2 (and_2_out, CWrite, ~Ii[15], clock);  // AND_Gate
  and and_3 (and_3_out, CWrite, Ii[14], clock);
  J_K_Flip_Flop j_k_ff_2 (
    .J(CEnable), .clk(j_k_ff_3_qn), .K(CEnable), .Q(Do[14]), .Qn(j_k_ff_2_qn), .preset(and_3_out),
    .reset(or_2_out));  // open: en
  or or_2 (or_2_out, CReset, and_4_out);
  and and_4 (and_4_out, CWrite, ~Ii[14], clock);  // AND_Gate
  and and_5 (and_5_out, CWrite, Ii[13], clock);
  J_K_Flip_Flop j_k_ff_3 (
    .J(CEnable), .clk(j_k_ff_4_qn), .K(CEnable), .Q(Do[13]), .Qn(j_k_ff_3_qn), .preset(and_5_out),
    .reset(or_3_out));  // open: en
  or or_3 (or_3_out, CReset, and_6_out);
  and and_6 (and_6_out, CWrite, ~Ii[13], clock);  // AND_Gate
  assign Oo = COut ? Do : 16'bz;  // Controlled_Buffer controlled_buffer_1
  J_K_Flip_Flop j_k_ff_4 (
    .J(CEnable), .clk(j_k_ff_5_qn), .K(CEnable), .Q(Do[12]), .Qn(j_k_ff_4_qn), .preset(and_7_out),
    .reset(or_4_out));  // open: en
  or or_4 (or_4_out, CReset, and_8_out);
  and and_7 (and_7_out, CWrite, Ii[12], clock);
  and and_8 (and_8_out, CWrite, ~Ii[12], clock);  // AND_Gate
  J_K_Flip_Flop j_k_ff_5 (
    .J(CEnable), .clk(j_k_ff_6_qn), .K(CEnable), .Q(Do[11]), .Qn(j_k_ff_5_qn), .preset(and_10_out),
    .reset(or_5_out));  // open: en
  or or_5 (or_5_out, CReset, and_9_out);
  and and_9 (and_9_out, CWrite, ~Ii[11], clock);  // AND_Gate
  and and_10 (and_10_out, CWrite, Ii[11], clock);
  J_K_Flip_Flop j_k_ff_6 (
    .J(CEnable), .clk(j_k_ff_7_qn), .K(CEnable), .Q(Do[10]), .Qn(j_k_ff_6_qn), .preset(and_11_out),
    .reset(or_6_out));  // open: en
  or or_6 (or_6_out, CReset, and_12_out);
  and and_11 (and_11_out, CWrite, Ii[10], clock);
  and and_12 (and_12_out, CWrite, ~Ii[10], clock);  // AND_Gate
  J_K_Flip_Flop j_k_ff_7 (
    .J(CEnable), .clk(j_k_ff_8_qn), .K(CEnable), .Q(Do[9]), .Qn(j_k_ff_7_qn), .preset(and_13_out),
    .reset(or_7_out));  // open: en
  or or_7 (or_7_out, CReset, and_14_out);
  and and_13 (and_13_out, CWrite, Ii[9], clock);
  and and_14 (and_14_out, CWrite, ~Ii[9], clock);  // AND_Gate
  or or_8 (or_8_out, CReset, and_16_out);
  and and_15 (and_15_out, CWrite, Ii[8], clock);
  J_K_Flip_Flop j_k_ff_8 (
    .J(CEnable), .clk(j_k_ff_9_qn), .K(CEnable), .Q(Do[8]), .Qn(j_k_ff_8_qn), .preset(and_15_out),
    .reset(or_8_out));  // open: en
  and and_16 (and_16_out, CWrite, ~Ii[8], clock);  // AND_Gate
  and and_17 (and_17_out, CWrite, Ii[7], clock);
  J_K_Flip_Flop j_k_ff_9 (
    .K(j_k_ff_10_qn), .Q(Do[7]), .Qn(j_k_ff_9_qn), .preset(and_17_out), .reset(or_9_out));  // open: J, clk, en
  or or_9 (or_9_out, CReset, and_18_out);
  and and_18 (and_18_out, CWrite, ~Ii[7], clock);  // AND_Gate
  and and_19 (and_19_out, CWrite, Ii[6], clock);
  J_K_Flip_Flop j_k_ff_10 (
    .J(CEnable), .clk(j_k_ff_11_qn), .K(CEnable), .Q(Do[6]), .Qn(j_k_ff_10_qn), .preset(and_19_out),
    .reset(or_10_out));  // open: en
  or or_10 (or_10_out, CReset, and_20_out);
  and and_20 (and_20_out, CWrite, ~Ii[6], clock);  // AND_Gate
  and and_21 (and_21_out, CWrite, Ii[5], clock);
  J_K_Flip_Flop j_k_ff_11 (
    .J(CEnable), .clk(j_k_ff_12_qn), .K(CEnable), .Q(Do[5]), .Qn(j_k_ff_11_qn), .preset(and_21_out),
    .reset(or_11_out));  // open: en
  or or_11 (or_11_out, CReset, and_22_out);
  and and_22 (and_22_out, CWrite, ~Ii[5], clock);  // AND_Gate
  J_K_Flip_Flop j_k_ff_12 (
    .J(CEnable), .clk(j_k_ff_13_qn), .K(CEnable), .Q(Do[4]), .Qn(j_k_ff_12_qn), .preset(and_24_out),
    .reset(or_12_out));  // open: en
  or or_12 (or_12_out, CReset, and_23_out);
  and and_23 (and_23_out, CWrite, ~Ii[4], clock);  // AND_Gate
  and and_24 (and_24_out, CWrite, Ii[4], clock);
  J_K_Flip_Flop j_k_ff_13 (
    .J(CEnable), .clk(j_k_ff_14_qn), .K(CEnable), .Q(Do[3]), .Qn(j_k_ff_13_qn), .preset(and_26_out),
    .reset(or_13_out));  // open: en
  or or_13 (or_13_out, CReset, and_25_out);
  and and_25 (and_25_out, CWrite, ~Ii[3], clock);  // AND_Gate
  and and_26 (and_26_out, CWrite, Ii[3], clock);
  J_K_Flip_Flop j_k_ff_14 (
    .J(CEnable), .clk(j_k_ff_15_qn), .K(CEnable), .Q(Do[2]), .Qn(j_k_ff_14_qn), .preset(and_28_out),
    .reset(or_14_out));  // open: en
  or or_14 (or_14_out, CReset, and_27_out);
  and and_27 (and_27_out, CWrite, ~Ii[2], clock);  // AND_Gate
  and and_28 (and_28_out, CWrite, Ii[2], clock);
  J_K_Flip_Flop j_k_ff_15 (
    .J(CEnable), .clk(j_k_ff_16_qn), .K(CEnable), .Q(Do[1]), .Qn(j_k_ff_15_qn), .preset(and_30_out),
    .reset(or_15_out));  // open: en
  or or_15 (or_15_out, CReset, and_29_out);
  and and_29 (and_29_out, CWrite, ~Ii[1], clock);  // AND_Gate
  and and_30 (and_30_out, CWrite, Ii[1], clock);
  or or_16 (or_16_out, CReset, and_32_out);
  and and_31 (and_31_out, CWrite, Ii[0], clock);
  J_K_Flip_Flop j_k_ff_16 (
    .J(CEnable), .clk(clock), .K(CEnable), .Q(Do[0]), .Qn(j_k_ff_16_qn), .preset(and_31_out),
    .reset(or_16_out));  // open: en
  and and_32 (and_32_out, CWrite, ~Ii[0], clock);  // AND_Gate
endmodule

module register_2bit (
  input  clock,
  input  load,
  input  reset,
  input  enable,
  input  [1:0] Ii,
  output [1:0] Oo,
  output [1:0] Do
);

  Register #(.width(2)) register_1 (.D(Ii), .en(load), .Q(Do), .clk(clock), .clr(reset));
  assign Oo = enable ? Do : 2'bz;  // Controlled_Buffer controlled_buffer_1
endmodule

module instruction_set (
  input  ZF,
  input  CF,
  input  OP0,
  input  OP1,
  input  OP2,
  input  OP3,
  input  OP4,
  input  Clear,
  input  Clock,
  output OI,
  output JP,
  output CO,
  output CE,
  output IR,
  output II,
  output RR,
  output RW,
  output MI,
  output BO,
  output BI,
  output SU,
  output EO,
  output AO,
  output AI,
  output HL,
  output FI,
  output CO_2,
  output CI,
  output WD,
  output CD,
  output S7,
  output S6,
  output S5,
  output S4,
  output S3,
  output S2,
  output S1,
  output S0
);

  wire n4bit_decoder_1_d7, not_1_out, not_2_out, or_1_out;
  wire [15:0] counter_1_oo;
  wire [31:19] rom_1_data;

  not not_1 (not_1_out, 1'b1);
  or or_1 (or_1_out, Clear, IR, n4bit_decoder_1_d7);
  not not_2 (not_2_out, Clock);
  counter counter_1 (
    .COut(1'b1), .CEnable(1'b1), .CWrite(not_1_out), .CReset(or_1_out), .clock(not_2_out), .Oo(counter_1_oo));  // open: Ii, Do
  _4bit_decoder u_4bit_decoder_1 (
    .Enable(1'b1), .A({counter_1_oo[0], counter_1_oo[1], counter_1_oo[2], counter_1_oo[3]}), .DF(S7),
    .DE(S6), .DD(S5), .DC(S4), .DB(S3), .DA(S2), .D9(S1), .D8(S0), .D7(n4bit_decoder_1_d7));  // open: D6, D5, D4, D3, D2, D1, D0
  ROM #(.addrWidth(10), .dataWidth(32)) rom_1 (
    .addr({OP4, OP3, OP2, OP1, OP0, CF, ZF, counter_1_oo[2:0]}),
    .data({rom_1_data[31:24], CD, WD, rom_1_data[21:19], CI, CO_2, FI, HL, AI, AO, EO, SU, BI, BO, MI, RW, RR, II, IR, CE, CO, JP, OI}),
    .sel(1'b1));

  // Notes on the sheet:
  //   display instructions
  //   contents of rom_1 (hex, n*v repeats v):
  //   104 68 10 5*0 104 68 10 5*0 104 68 10 5*0 104 68 10 5*0 104 68 8000 10 4*0 104 68 8000 10 4*0 104 68
  //   8000 10 4*0 104 68 8000 10 4*0 104 68 10c 4040 10 0 0 0 104 68 10c 4040 10 0 0 0 104 68 10c 4040 10
  //   0 0 0 104 68 10c 4040 10 0 0 0 104 68 10c 140 4040 10 0 0 104 68 10c 140 4040 10 0 0 104 68 10c 140
  //   4040 10 0 0 104 68 10c 140 4040 10 0 0 104 68 10c 140 2080 10 0 0 104 68 10c 140 2080 10 0 0 104 68
  //   10c 140 2080 10 0 0 104 68 10c 140 2080 10 0 0 104 68 10c 440 10 0 0 0 104 68 10c 440 10 0 0 0 104
  //   68 10c 440 10 0 0 0 104 68 10c 440 10 0 0 0 104 68 10c 140 440 10 0 0 104 68 10c 140 440 10 0 0 104
  //   68 10c 140 440 10 0 0 104 68 10c 140 440 10 0 0 104 68 10c 140 280 10 0 0 104 68 10c 140 280 10 0 0
  //   104 68 10c 140 280 10 0 0 104 68 10c 140 280 10 0 0 104 68 10c 440 15000 10 0 0 104 68 10c 440 15000
  //   10 0 0 104 68 10c 440 15000 10 0 0 104 68 10c 440 15000 10 0 0 104 68 10c 140 440 15000 10 0 104 68
  //   10c 140 440 15000 10 0 104 68 10c 140 440 15000 10 0 104 68 10c 140 440 15000 10 0 104 68 10c c40
  //   15800 10 0 0 104 68 10c c40 15800 10 0 0 104 68 10c c40 15800 10 0 0 104 68 10c c40 15800 10 0 0 104
  //   68 10c 140 c40 15800 10 0 104 68 10c 140 c40 15800 10 0 104 68 10c 140 c40 15800 10 0 104 68 10c 140
  //   c40 15800 10 0 104 68 2001 10 4*0 104 68 2001 10 4*0 104 68 2001 10 4*0 104 68 2001 10 4*0 104 68
  //   201 10 4*0 104 68 201 10 4*0 104 68 201 10 4*0 104 68 201 10 4*0 104 68 10c 41 10 0 0 0 104 68 10c
  //   41 10 0 0 0 104 68 10c 41 10 0 0 0 104 68 10c 41 10 0 0 0 104 68 10c 140 41 10 0 0 104 68 10c 140 41
  //   10 0 0 104 68 10c 140 41 10 0 0 104 68 10c 140 41 10 0 0 104 68 40004 10c 42 10 0 0 104 68 40004 10c
  //   42 10 0 0 104 68 40004 10c 42 10 0 0 104 68 40004 10c 42 10 0 0 104 68 8 10 4*0 104 68 40004 10c 42
  //   10 0 0 104 68 8 10 4*0 104 68 40004 10c 42 10 0 0 104 68 8 10 4*0 104 68 8 10 4*0 104 68 40004 10c
  //   42 10 0 0 104 68 40004 10c 42 10 0 0 104 68 20002 10 4*0 104 68 20002 10 4*0 104 68 20002 10 4*0 104
  //   68 20002 10 4*0 104 68 10c 42 10 0 0 0 104 68 10c 42 10 0 0 0 104 68 10c 42 10 0 0 0 104 68 10c 42
  //   10 0 0 0 104 68 8 10 4*0 104 68 10c 42 10 0 0 0 104 68 8 10 4*0 104 68 10c 42 10 0 0 0 104 68 8 10
  //   4*0 104 68 8 10 4*0 104 68 10c 42 10 0 0 0 104 68 10c 42 10 0 0 0 104 68 0 10 4*0 104 68 0 10 4*0
  //   104 68 20002 10 4*0 104 68 20002 10 4*0 104 68 0 10 4*0 104 68 20002 10 4*0 104 68 0 10 4*0 104 68
  //   20002 10 4*0 104 68 10c 40040 10 0 0 0 104 68 10c 40040 10 0 0 0 104 68 10c 40040 10 0 0 0 104 68
  //   10c 40040 10 0 0 0 104 68 10c 140 40040 10 0 0 104 68 10c 140 40040 10 0 0 104 68 10c 140 40040 10 0
  //   0 104 68 10c 140 40040 10 0 0 104 68 10c 140 20080 10 0 0 104 68 10c 140 20080 10 0 0 104 68 10c 140
  //   20080 10 0 0 104 68 10c 140 20080 10
endmodule

module _4bit_decoder (
  input  Enable,
  input  [3:0] A,
  output DF,
  output DE,
  output DD,
  output DC,
  output DB,
  output DA,
  output D9,
  output D8,
  output D7,
  output D6,
  output D5,
  output D4,
  output D3,
  output D2,
  output D1,
  output D0
);

  wire and_1_out, and_2_out, and_3_out, and_4_out, and_5_out, and_6_out, and_7_out, and_8_out, and_9_out,
       and_10_out, and_11_out, and_12_out, and_13_out, and_14_out, and_15_out, and_16_out, not_1_out,
       not_2_out, not_3_out, not_4_out;

  not not_1 (not_1_out, A[3]);
  not not_2 (not_2_out, A[2]);
  not not_3 (not_3_out, A[1]);
  not not_4 (not_4_out, A[0]);
  assign DF = Enable ? and_16_out : 1'bz;  // Controlled_Buffer controlled_buffer_1
  and and_1 (and_1_out, not_1_out, not_2_out, not_3_out, not_4_out);
  and and_2 (and_2_out, not_1_out, not_2_out, not_3_out, A[0]);
  and and_3 (and_3_out, not_1_out, not_2_out, A[1], not_4_out);
  and and_4 (and_4_out, not_1_out, not_2_out, A[1], A[0]);
  and and_5 (and_5_out, not_1_out, A[2], not_3_out, not_4_out);
  and and_6 (and_6_out, not_1_out, A[2], not_3_out, A[0]);
  and and_7 (and_7_out, not_1_out, A[2], A[1], not_4_out);
  and and_8 (and_8_out, not_1_out, A[2], A[1], A[0]);
  and and_9 (and_9_out, A[3], not_2_out, not_3_out, not_4_out);
  and and_10 (and_10_out, A[3], not_2_out, not_3_out, A[0]);
  and and_11 (and_11_out, A[3], not_2_out, A[1], not_4_out);
  and and_12 (and_12_out, A[3], not_2_out, A[1], A[0]);
  and and_13 (and_13_out, A[3], A[2], not_3_out, not_4_out);
  and and_14 (and_14_out, A[3], A[2], not_3_out, A[0]);
  and and_15 (and_15_out, A[3], A[2], A[1], not_4_out);
  and and_16 (and_16_out, A[3], A[2], A[1], A[0]);
  assign DE = Enable ? and_15_out : 1'bz;  // Controlled_Buffer controlled_buffer_2
  assign DC = Enable ? and_13_out : 1'bz;  // Controlled_Buffer controlled_buffer_3
  assign DB = Enable ? and_12_out : 1'bz;  // Controlled_Buffer controlled_buffer_4
  assign DD = Enable ? and_14_out : 1'bz;  // Controlled_Buffer controlled_buffer_5
  assign D8 = Enable ? and_9_out : 1'bz;  // Controlled_Buffer controlled_buffer_6
  assign DA = Enable ? and_11_out : 1'bz;  // Controlled_Buffer controlled_buffer_7
  assign D7 = Enable ? and_8_out : 1'bz;  // Controlled_Buffer controlled_buffer_8
  assign D9 = Enable ? and_10_out : 1'bz;  // Controlled_Buffer controlled_buffer_9
  assign D6 = Enable ? and_7_out : 1'bz;  // Controlled_Buffer controlled_buffer_10
  assign D5 = Enable ? and_6_out : 1'bz;  // Controlled_Buffer controlled_buffer_11
  assign D4 = Enable ? and_5_out : 1'bz;  // Controlled_Buffer controlled_buffer_12
  assign D3 = Enable ? and_4_out : 1'bz;  // Controlled_Buffer controlled_buffer_13
  assign D0 = Enable ? and_1_out : 1'bz;  // Controlled_Buffer controlled_buffer_14
  assign D1 = Enable ? and_2_out : 1'bz;  // Controlled_Buffer controlled_buffer_15
  assign D2 = Enable ? and_3_out : 1'bz;  // Controlled_Buffer controlled_buffer_16
endmodule

module _7_segment (
  input  [15:0] I,
  output out_2,
  output out_3,
  output out_4,
  output out_5,
  output out_6,
  output out_7,
  output out_8,
  output out_9,
  output out_10,
  output out_11,
  output out_12,
  output out_13,
  output out_14,
  output out_15,
  output out_16,
  output out_17,
  output out_18,
  output out_19,
  output out_20,
  output out_21,
  output out_22,
  output out_23,
  output out_24,
  output out_25,
  output out_26,
  output out_27,
  output out_28,
  output out_29
);

  ROM #(.addrWidth(16), .dataWidth(28)) rom_1 (
    .addr(I),
    .data({out_29, out_28, out_27, out_26, out_25, out_24, out_23, out_22, out_21, out_20, out_19, out_18, out_17, out_16, out_15, out_14, out_13, out_12, out_11, out_10, out_9, out_8, out_7, out_6, out_5, out_4, out_3, out_2}),
    .sel(1'b1));

  // Notes on the sheet:
  //   contents of rom_1 (hex, n*v repeats v):
  //   3f 6 5b 4f 66 6d 7d 7 7f 6f 33f 306 35b 34f 366 36d 37d 307 37f 36f 2dbf 2d86 2ddb 2dcf 2de6 2ded
  //   2dfd 2d87 2dff 2def 27bf 2786 27db 27cf 27e6 27ed 27fd 2787 27ff 27ef 333f 3306 335b 334f 3366 336d
  //   337d 3307 337f 336f 36bf 3686 36db 36cf 36e6 36ed 36fd 3687 36ff 36ef 3ebf 3e86 3edb 3ecf 3ee6 3eed
  //   3efd 3e87 3eff 3eef 3bf 386 3db 3cf 3e6 3ed 3fd 387 3ff 3ef 3fbf 3f86 3fdb 3fcf 3fe6 3fed 3ffd 3f87
  //   3fff 3fef 37bf 3786 37db 37cf 37e6 37ed 37fd 3787 37ff 37ef 19fbf 19f86 19fdb 19fcf 19fe6 19fed
  //   19ffd 19f87 19fff 19fef 1833f 18306 1835b 1834f 18366 1836d 1837d 18307 1837f 1836f 1adbf 1ad86
  //   1addb 1adcf 1ade6 1aded 1adfd 1ad87 1adff 1adef 1a7bf 1a786 1a7db 1a7cf 1a7e6 1a7ed 1a7fd 1a787
  //   1a7ff 1a7ef 1b33f 1b306 1b35b 1b34f 1b366 1b36d 1b37d 1b307 1b37f 1b36f 1b6bf 1b686 1b6db 1b6cf
  //   1b6e6 1b6ed 1b6fd 1b687 1b6ff 1b6ef 1bebf 1be86 1bedb 1becf 1bee6 1beed 1befd 1be87 1beff 1beef
  //   183bf 18386 183db 183cf 183e6 183ed 183fd 18387 183ff 183ef 1bfbf 1bf86 1bfdb 1bfcf 1bfe6 1bfed
  //   1bffd 1bf87 1bfff 1bfef 1b7bf 1b786 1b7db 1b7cf 1b7e6 1b7ed 1b7fd 1b787 1b7ff 1b7ef 16dfbf 16df86
  //   16dfdb 16dfcf 16dfe6 16dfed 16dffd 16df87 16dfff 16dfef 16c33f 16c306 16c35b 16c34f 16c366 16c36d
  //   16c37d 16c307 16c37f 16c36f 16edbf 16ed86 16eddb 16edcf 16ede6 16eded 16edfd 16ed87 16edff 16edef
  //   16e7bf 16e786 16e7db 16e7cf 16e7e6 16e7ed 16e7fd 16e787 16e7ff 16e7ef 16f33f 16f306 16f35b 16f34f
  //   16f366 16f36d 16f37d 16f307 16f37f 16f36f 16f6bf 16f686 16f6db 16f6cf 16f6e6 16f6ed 16f6fd 16f687
  //   16f6ff 16f6ef 16febf 16fe86 16fedb 16fecf 16fee6 16feed 16fefd 16fe87 16feff 16feef 16c3bf 16c386
  //   16c3db 16c3cf 16c3e6 16c3ed 16c3fd 16c387 16c3ff 16c3ef 16ffbf 16ff86 16ffdb 16ffcf 16ffe6 16ffed
  //   16fffd 16ff87 16ffff 16ffef 16f7bf 16f786 16f7db 16f7cf 16f7e6 16f7ed 16f7fd 16f787 16f7ff 16f7ef
  //   13dfbf 13df86 13dfdb 13dfcf 13dfe6 13dfed 13dffd 13df87 13dfff 13dfef 13c33f 13c306 13c35b 13c34f
  //   13c366 13c36d 13c37d 13c307 13c37f 13c36f 13edbf 13ed86 13eddb 13edcf 13ede6 13eded 13edfd 13ed87
  //   13edff 13edef 13e7bf 13e786 13e7db 13e7cf 13e7e6 13e7ed 13e7fd 13e787 13e7ff 13e7ef 13f33f 13f306
  //   13f35b 13f34f 13f366 13f36d 13f37d 13f307 13f37f 13f36f 13f6bf 13f686 13f6db 13f6cf 13f6e6 13f6ed
  //   13f6fd 13f687 13f6ff 13f6ef 13febf 13fe86 13fedb 13fecf 13fee6 13feed 13fefd 13fe87 13feff 13feef
  //   13c3bf 13c386 13c3db 13c3cf 13c3e6 13c3ed 13c3fd 13c387 13c3ff 13c3ef 13ffbf 13ff86 13ffdb 13ffcf
  //   13ffe6 13ffed 13fffd 13ff87 13ffff 13ffef 13f7bf 13f786 13f7db 13f7cf 13f7e6 13f7ed 13f7fd 13f787
  //   13f7ff 13f7ef 199fbf 199f86 199fdb 199fcf 199fe6 199fed 199ffd 199f87 199fff 199fef 19833f 198306
  //   19835b 19834f 198366 19836d 19837d 198307 19837f 19836f 19adbf 19ad86 19addb 19adcf 19ade6 19aded
  //   19adfd 19ad87 19adff 19adef 19a7bf 19a786 19a7db 19a7cf 19a7e6 19a7ed 19a7fd 19a787 19a7ff 19a7ef
  //   19b33f 19b306 19b35b 19b34f 19b366 19b36d 19b37d 19b307 19b37f 19b36f 19b6bf 19b686 19b6db 19b6cf
  //   19b6e6 19b6ed 19b6fd 19b687 19b6ff 19b6ef 19bebf 19be86 19bedb 19becf 19bee6 19beed 19befd 19be87
  //   19beff 19beef 1983bf 198386 1983db 1983cf 1983e6 1983ed 1983fd 198387 1983ff 1983ef 19bfbf 19bf86
  //   19bfdb 19bfcf 19bfe6 19bfed 19bffd 19bf87 19bfff 19bfef 19b7bf 19b786 19b7db 19b7cf 19b7e6 19b7ed
  //   19b7fd 19b787 19b7ff 19b7ef 1b5fbf 1b5f86 1b5fdb 1b5fcf 1b5fe6 1b5fed 1b5ffd 1b5f87 1b5fff 1b5fef
  //   1b433f 1b4306 1b435b 1b434f 1b4366 1b436d 1b437d 1b4307 1b437f 1b436f 1b6dbf 1b6d86 1b6ddb 1b6dcf
  //   1b6de6 1b6ded 1b6dfd 1b6d87 1b6dff 1b6def 1b67bf 1b6786 1b67db 1b67cf 1b67e6 1b67ed 1b67fd 1b6787
  //   1b67ff 1b67ef 1b733f 1b7306 1b735b 1b734f 1b7366 1b736d 1b737d 1b7307 1b737f 1b736f 1b76bf 1b7686
  //   1b76db 1b76cf 1b76e6 1b76ed 1b76fd 1b7687 1b76ff 1b76ef 1b7ebf 1b7e86 1b7edb 1b7ecf 1b7ee6 1b7eed
  //   1b7efd 1b7e87 1b7eff 1b7eef 1b43bf 1b4386 1b43db 1b43cf 1b43e6 1b43ed 1b43fd 1b4387 1b43ff 1b43ef
  //   1b7fbf 1b7f86 1b7fdb 1b7fcf 1b7fe6 1b7fed 1b7ffd 1b7f87 1b7fff 1b7fef 1b77bf 1b7786 1b77db 1b77cf
  //   1b77e6 1b77ed 1b77fd 1b7787 1b77ff 1b77ef 1f5fbf 1f5f86 1f5fdb 1f5fcf 1f5fe6 1f5fed 1f5ffd 1f5f87
  //   1f5fff 1f5fef 1f433f 1f4306 1f435b 1f434f 1f4366 1f436d 1f437d 1f4307 1f437f 1f436f 1f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
endmodule

module display_instruction_set (
  input  Clock,
  input  Clear,
  input  [15:0] in_3,
  output [6:0] ACSII_Output,
  output [15:0] Full_Output,
  output [3:0] Position_Output
);

  wire [6:0] rom_2_data;
  wire [7:4] counter_1_q;
  wire [15:0] rom_1_data;

  Counter counter_1 (
    .count(1'b1), .Q({counter_1_q, Position_Output}), .clk(Clock), .clr(Clear));  // open: load, D, carry
  ROM #(.addrWidth(16), .dataWidth(16)) rom_1 (
    .addr({in_3[7:0], counter_1_q, Position_Output}), .data(rom_1_data), .sel(1'b1));
  ROM #(.addrWidth(16), .dataWidth(7)) rom_2 (.data(rom_2_data), .sel(1'b1));  // open: addr
endmodule

module display_register (
  input  Clock,
  input  Enabled,
  input  Clear,
  input  ClearAll,
  input  [15:0] in_5,
  input  [3:0] in_6,
  output [15:0] out_7,
  output [15:0] out_8,
  output [15:0] out_9,
  output [15:0] out_10,
  output [15:0] out_11,
  output [15:0] out_12,
  output [15:0] out_13,
  output [15:0] out_14,
  output [15:0] out_15,
  output [15:0] out_16,
  output [15:0] out_17,
  output [15:0] out_18,
  output [15:0] out_19,
  output [15:0] out_20,
  output [15:0] out_21,
  output [15:0] out_22
);

  wire and_1_out, and_2_out, and_3_out, and_4_out, and_5_out, and_6_out, and_7_out, and_8_out, and_9_out,
       and_10_out, and_11_out, and_12_out, and_13_out, and_14_out, and_15_out, and_16_out,
       n4bit_decoder_1_d0, n4bit_decoder_1_d1, n4bit_decoder_1_d2, n4bit_decoder_1_d3, n4bit_decoder_1_d4,
       n4bit_decoder_1_d5, n4bit_decoder_1_d6, n4bit_decoder_1_d7, n4bit_decoder_1_d8, n4bit_decoder_1_d9,
       n4bit_decoder_1_da, n4bit_decoder_1_db, n4bit_decoder_1_dc, n4bit_decoder_1_dd, n4bit_decoder_1_de,
       n4bit_decoder_1_df, or_1_out, or_2_out, or_3_out, or_4_out, or_5_out, or_6_out, or_7_out, or_8_out,
       or_9_out, or_10_out, or_11_out, or_12_out, or_13_out, or_14_out, or_15_out, or_16_out;
  wire [15:0] controlled_buffer_1_out, controlled_buffer_2_out, controlled_buffer_3_out,
       controlled_buffer_4_out, controlled_buffer_5_out, controlled_buffer_6_out, controlled_buffer_7_out,
       controlled_buffer_8_out, controlled_buffer_9_out, controlled_buffer_10_out, controlled_buffer_11_out,
       controlled_buffer_12_out, controlled_buffer_13_out, controlled_buffer_14_out,
       controlled_buffer_15_out, controlled_buffer_16_out;

  _4bit_decoder u_4bit_decoder_1 (
    .Enable(1'b1), .A(in_6), .DF(n4bit_decoder_1_df), .DE(n4bit_decoder_1_de), .DD(n4bit_decoder_1_dd),
    .DC(n4bit_decoder_1_dc), .DB(n4bit_decoder_1_db), .DA(n4bit_decoder_1_da), .D9(n4bit_decoder_1_d9),
    .D8(n4bit_decoder_1_d8), .D7(n4bit_decoder_1_d7), .D6(n4bit_decoder_1_d6), .D5(n4bit_decoder_1_d5),
    .D4(n4bit_decoder_1_d4), .D3(n4bit_decoder_1_d3), .D2(n4bit_decoder_1_d2), .D1(n4bit_decoder_1_d1),
    .D0(n4bit_decoder_1_d0));
  Register #(.width(16)) register_1 (.D(controlled_buffer_1_out), .en(Enabled), .Q(out_7), .clk(Clock), .clr(or_1_out));
  or or_1 (or_1_out, and_1_out, ClearAll);
  and and_1 (and_1_out, Clear, n4bit_decoder_1_d0);
  assign controlled_buffer_1_out = n4bit_decoder_1_d0 ? in_5 : 16'bz;  // Controlled_Buffer controlled_buffer_1
  or or_2 (or_2_out, and_2_out, ClearAll);
  and and_2 (and_2_out, Clear, n4bit_decoder_1_d1);
  assign controlled_buffer_2_out = n4bit_decoder_1_d1 ? in_5 : 16'bz;  // Controlled_Buffer controlled_buffer_2
  Register #(.width(16)) register_2 (.D(controlled_buffer_2_out), .en(Enabled), .Q(out_8), .clk(Clock), .clr(or_2_out));
  and and_3 (and_3_out, Clear, n4bit_decoder_1_d2);
  assign controlled_buffer_3_out = n4bit_decoder_1_d2 ? in_5 : 16'bz;  // Controlled_Buffer controlled_buffer_3
  Register #(.width(16)) register_3 (.D(controlled_buffer_3_out), .en(Enabled), .Q(out_9), .clk(Clock), .clr(or_3_out));
  or or_3 (or_3_out, and_3_out, ClearAll);
  assign controlled_buffer_4_out = n4bit_decoder_1_d3 ? in_5 : 16'bz;  // Controlled_Buffer controlled_buffer_4
  Register #(.width(16)) register_4 (
    .D(controlled_buffer_4_out), .en(Enabled), .Q(out_10), .clk(Clock), .clr(or_4_out));
  or or_4 (or_4_out, and_4_out, ClearAll);
  and and_4 (and_4_out, Clear, n4bit_decoder_1_d3);
  assign controlled_buffer_5_out = n4bit_decoder_1_d4 ? in_5 : 16'bz;  // Controlled_Buffer controlled_buffer_5
  Register #(.width(16)) register_5 (
    .D(controlled_buffer_5_out), .en(Enabled), .Q(out_11), .clk(Clock), .clr(or_5_out));
  or or_5 (or_5_out, and_5_out, ClearAll);
  and and_5 (and_5_out, Clear, n4bit_decoder_1_d4);
  assign controlled_buffer_6_out = n4bit_decoder_1_d5 ? in_5 : 16'bz;  // Controlled_Buffer controlled_buffer_6
  Register #(.width(16)) register_6 (
    .D(controlled_buffer_6_out), .en(Enabled), .Q(out_12), .clk(Clock), .clr(or_6_out));
  or or_6 (or_6_out, and_6_out, ClearAll);
  and and_6 (and_6_out, Clear, n4bit_decoder_1_d5);
  Register #(.width(16)) register_7 (
    .D(controlled_buffer_7_out), .en(Enabled), .Q(out_13), .clk(Clock), .clr(or_7_out));
  or or_7 (or_7_out, and_7_out, ClearAll);
  and and_7 (and_7_out, Clear, n4bit_decoder_1_d6);
  assign controlled_buffer_7_out = n4bit_decoder_1_d6 ? in_5 : 16'bz;  // Controlled_Buffer controlled_buffer_7
  Register #(.width(16)) register_8 (
    .D(controlled_buffer_8_out), .en(Enabled), .Q(out_14), .clk(Clock), .clr(or_8_out));
  or or_8 (or_8_out, and_8_out, ClearAll);
  and and_8 (and_8_out, Clear, n4bit_decoder_1_d7);
  assign controlled_buffer_8_out = n4bit_decoder_1_d7 ? in_5 : 16'bz;  // Controlled_Buffer controlled_buffer_8
  Register #(.width(16)) register_9 (
    .D(controlled_buffer_9_out), .en(Enabled), .Q(out_15), .clk(Clock), .clr(or_9_out));
  or or_9 (or_9_out, and_9_out, ClearAll);
  and and_9 (and_9_out, Clear, n4bit_decoder_1_d8);
  assign controlled_buffer_9_out = n4bit_decoder_1_d8 ? in_5 : 16'bz;  // Controlled_Buffer controlled_buffer_9
  or or_10 (or_10_out, and_10_out, ClearAll);
  and and_10 (and_10_out, Clear, n4bit_decoder_1_d9);
  assign controlled_buffer_10_out = n4bit_decoder_1_d9 ? in_5 : 16'bz;  // Controlled_Buffer controlled_buffer_10
  Register #(.width(16)) register_10 (
    .D(controlled_buffer_10_out), .en(Enabled), .Q(out_16), .clk(Clock), .clr(or_10_out));
  and and_11 (and_11_out, Clear, n4bit_decoder_1_da);
  assign controlled_buffer_11_out = n4bit_decoder_1_da ? in_5 : 16'bz;  // Controlled_Buffer controlled_buffer_11
  Register #(.width(16)) register_11 (
    .D(controlled_buffer_11_out), .en(Enabled), .Q(out_17), .clk(Clock), .clr(or_11_out));
  or or_11 (or_11_out, and_11_out, ClearAll);
  assign controlled_buffer_12_out = n4bit_decoder_1_db ? in_5 : 16'bz;  // Controlled_Buffer controlled_buffer_12
  Register #(.width(16)) register_12 (
    .D(controlled_buffer_12_out), .en(Enabled), .Q(out_18), .clk(Clock), .clr(or_12_out));
  or or_12 (or_12_out, and_12_out, ClearAll);
  and and_12 (and_12_out, Clear, n4bit_decoder_1_db);
  assign controlled_buffer_13_out = n4bit_decoder_1_dc ? in_5 : 16'bz;  // Controlled_Buffer controlled_buffer_13
  Register #(.width(16)) register_13 (
    .D(controlled_buffer_13_out), .en(Enabled), .Q(out_19), .clk(Clock), .clr(or_13_out));
  or or_13 (or_13_out, and_13_out, ClearAll);
  and and_13 (and_13_out, Clear, n4bit_decoder_1_dc);
  assign controlled_buffer_14_out = n4bit_decoder_1_dd ? in_5 : 16'bz;  // Controlled_Buffer controlled_buffer_14
  Register #(.width(16)) register_14 (
    .D(controlled_buffer_14_out), .en(Enabled), .Q(out_20), .clk(Clock), .clr(or_14_out));
  or or_14 (or_14_out, and_14_out, ClearAll);
  and and_14 (and_14_out, Clear, n4bit_decoder_1_dd);
  Register #(.width(16)) register_15 (
    .D(controlled_buffer_15_out), .en(Enabled), .Q(out_21), .clk(Clock), .clr(or_15_out));
  or or_15 (or_15_out, and_15_out, ClearAll);
  and and_15 (and_15_out, Clear, n4bit_decoder_1_de);
  assign controlled_buffer_15_out = n4bit_decoder_1_de ? in_5 : 16'bz;  // Controlled_Buffer controlled_buffer_15
  Register #(.width(16)) register_16 (
    .D(controlled_buffer_16_out), .en(Enabled), .Q(out_22), .clk(Clock), .clr(or_16_out));
  or or_16 (or_16_out, and_16_out, ClearAll);
  and and_16 (and_16_out, Clear, n4bit_decoder_1_df);
  assign controlled_buffer_16_out = n4bit_decoder_1_df ? in_5 : 16'bz;  // Controlled_Buffer controlled_buffer_16
endmodule

module CPU (
);

  wire n7_segment_1_out_2, n7_segment_1_out_3, n7_segment_1_out_4, n7_segment_1_out_5, n7_segment_1_out_6,
       n7_segment_1_out_7, n7_segment_1_out_8, n7_segment_1_out_9, n7_segment_1_out_10, n7_segment_1_out_11,
       n7_segment_1_out_12, n7_segment_1_out_13, n7_segment_1_out_14, n7_segment_1_out_15,
       n7_segment_1_out_16, n7_segment_1_out_17, n7_segment_1_out_18, n7_segment_1_out_19,
       n7_segment_1_out_20, n7_segment_1_out_21, n7_segment_1_out_22, n7_segment_1_out_23,
       n7_segment_1_out_24, n7_segment_1_out_25, n7_segment_1_out_26, n7_segment_1_out_27,
       n7_segment_1_out_28, n7_segment_1_out_29, Reset_out, Reset_RAM_out;
  wire [15:0] main_1__7_segment_output;

  Button Reset_RAM (.out(Reset_RAM_out));
  Button Reset (.out(Reset_out));
  _7_Segment_Display u_7_segment_display_1 (
    .g(n7_segment_1_out_29), .f(n7_segment_1_out_28), .a(n7_segment_1_out_23), .b(n7_segment_1_out_24),
    .e(n7_segment_1_out_27), .d(n7_segment_1_out_26), .c(n7_segment_1_out_25));  // open: dp
  main main_1 (.Reset_RAM(Reset_RAM_out), .Reset_System(Reset_out), ._7_Segment_Output(main_1__7_segment_output));
  _7_Segment_Display u_7_segment_display_2 (
    .g(n7_segment_1_out_22), .f(n7_segment_1_out_21), .a(n7_segment_1_out_16), .b(n7_segment_1_out_17),
    .e(n7_segment_1_out_20), .d(n7_segment_1_out_19), .c(n7_segment_1_out_18));  // open: dp
  _7_segment u_7_segment_1 (
    .I(main_1__7_segment_output), .out_9(n7_segment_1_out_9), .out_10(n7_segment_1_out_10),
    .out_11(n7_segment_1_out_11), .out_12(n7_segment_1_out_12), .out_13(n7_segment_1_out_13),
    .out_14(n7_segment_1_out_14), .out_15(n7_segment_1_out_15), .out_16(n7_segment_1_out_16),
    .out_17(n7_segment_1_out_17), .out_18(n7_segment_1_out_18), .out_19(n7_segment_1_out_19),
    .out_20(n7_segment_1_out_20), .out_21(n7_segment_1_out_21), .out_22(n7_segment_1_out_22),
    .out_23(n7_segment_1_out_23), .out_24(n7_segment_1_out_24), .out_25(n7_segment_1_out_25),
    .out_26(n7_segment_1_out_26), .out_27(n7_segment_1_out_27), .out_28(n7_segment_1_out_28),
    .out_29(n7_segment_1_out_29), .out_2(n7_segment_1_out_2), .out_3(n7_segment_1_out_3),
    .out_4(n7_segment_1_out_4), .out_5(n7_segment_1_out_5), .out_6(n7_segment_1_out_6),
    .out_7(n7_segment_1_out_7), .out_8(n7_segment_1_out_8));
  _7_Segment_Display u_7_segment_display_3 (
    .g(n7_segment_1_out_8), .f(n7_segment_1_out_7), .a(n7_segment_1_out_2), .b(n7_segment_1_out_3),
    .e(n7_segment_1_out_6), .d(n7_segment_1_out_5), .c(n7_segment_1_out_4));  // open: dp
  _7_Segment_Display u_7_segment_display_4 (
    .g(n7_segment_1_out_15), .f(n7_segment_1_out_14), .a(n7_segment_1_out_9), .b(n7_segment_1_out_10),
    .e(n7_segment_1_out_13), .d(n7_segment_1_out_12), .c(n7_segment_1_out_11));  // open: dp
endmodule
